// Logisim project incrementadores_contadores_divisores_de_clock.circ as structural Verilog: 8 circuits, main circuit Contador de 4 bits
module Contador_de_4_bits (
  input  Enable,
  input  Clear,
  input  CLOCK,
  output q3,
  output q2,
  output q1,
  output q0
);

  wire [3:0] Incrementador_s0;

  Register #(.width(4), .Select("low")) register_1 (
    .D(Incrementador_s0), .en(Enable), .Q({q3, q2, q1, q0}), .clk(CLOCK), .clr(Clear), .cs(1'b0),
    .preset(1'b0));
  Incrementador_de_4_bits Incrementador (
    .s0(Incrementador_s0[0]), .s1(Incrementador_s0[1]), .s2(Incrementador_s0[2]), .s3(Incrementador_s0[3]),
    .a0(q0), .a1(q1), .a2(q2), .a3(q3));  // open: c0
endmodule

module Meio_Somador (
  input  a,
  input  b,
  output s,
  output c0
);

  xor xor_1 (s, a, b);
  and and_1 (c0, a, b);
endmodule

module Incrementador_de_4_bits (
  input  a0,
  input  a1,
  input  a2,
  input  a3,
  output s0,
  output s1,
  output s2,
  output s3,
  output c0
);

  wire meio_somador_1_c0, meio_somador_2_c0, meio_somador_3_c0;

  Meio_Somador meio_somador_1 (.a(1'b1), .b(a0), .s(s0), .c0(meio_somador_1_c0));
  Meio_Somador meio_somador_2 (.a(meio_somador_1_c0), .b(a1), .s(s1), .c0(meio_somador_2_c0));
  Meio_Somador meio_somador_3 (.a(meio_somador_2_c0), .b(a2), .s(s2), .c0(meio_somador_3_c0));
  Meio_Somador meio_somador_4 (.a(meio_somador_3_c0), .b(a3), .s(s3), .c0(c0));
endmodule

module Divisor_de_clock___cascata (
  input  Enable,
  input  Clear,
  output CLOCK_OUT
);

  wire CLOCK_IN_out, \Estágio_1_clock_out , \Estágio_2_clock_out , \Estágio_3_clock_out ,
       \Estágio_4_clock_out , \Estágio_5_clock_out , \Estágio_6_clock_out ;

  Divisor_de_clock___divide_por_16 \Estágio_1  (
    .Enable(Enable), .CLOCK_IN(CLOCK_IN_out), .Clear(Clear), .CLOCK_OUT(\Estágio_1_clock_out ));
  Clock CLOCK_IN (.out(CLOCK_IN_out));
  Divisor_de_clock___divide_por_16 \Estágio_2  (
    .Enable(Enable), .CLOCK_IN(\Estágio_1_clock_out ), .Clear(Clear), .CLOCK_OUT(\Estágio_2_clock_out ));
  Divisor_de_clock___divide_por_16 \Estágio_3  (
    .Enable(Enable), .CLOCK_IN(\Estágio_2_clock_out ), .Clear(Clear), .CLOCK_OUT(\Estágio_3_clock_out ));
  Divisor_de_clock___divide_por_16 \Estágio_4  (
    .Enable(Enable), .CLOCK_IN(\Estágio_3_clock_out ), .Clear(Clear), .CLOCK_OUT(\Estágio_4_clock_out ));
  Divisor_de_clock___divide_por_16 \Estágio_5  (
    .Enable(Enable), .CLOCK_IN(\Estágio_4_clock_out ), .Clear(Clear), .CLOCK_OUT(\Estágio_5_clock_out ));
  Divisor_de_clock___divide_por_16 \Estágio_6  (
    .Enable(Enable), .CLOCK_IN(\Estágio_5_clock_out ), .Clear(Clear), .CLOCK_OUT(\Estágio_6_clock_out ));
  Divisor_de_clock___divide_por_16 divisor_de_clock_divide_por_16_1 (
    .Enable(Enable), .CLOCK_IN(\Estágio_6_clock_out ), .Clear(Clear), .CLOCK_OUT(CLOCK_OUT));

  // Notes on the sheet:
  //   Estágio 7(divisor por 3)
endmodule

module Divisor_de_clock___divide_por_16 (
  input  Enable,
  input  CLOCK_IN,
  input  Clear,
  output CLOCK_OUT
);

  Contador_de_4_bits contador_de_4_bits_1 (
    .Enable(Enable), .CLOCK(CLOCK_IN), .q3(CLOCK_OUT), .Clear(Clear));  // open: q2, q1, q0
  // Digital_Oscilloscope #(.nState(15)) CLOCK_IN_em_cima__x_CLOCK_OUT_embaixo: pin names not known; wires that end beside it: CLOCK_IN, CLOCK_OUT, 1'b1, 1'b0
endmodule

module Incrementador_de_2_bits (
  input  a0,
  input  a1,
  output s0,
  output s1,
  output c0
);

  wire meio_somador_2_c0;

  Meio_Somador meio_somador_1 (.a(meio_somador_2_c0), .b(a1), .s(s1), .c0(c0));
  Meio_Somador meio_somador_2 (.a(1'b1), .b(a0), .s(s0), .c0(meio_somador_2_c0));
endmodule

module Contador_de_2_bits (
  input  Enable,
  input  Clear,
  input  CLOCK_IN,
  output q1,
  output q0
);

  wire [1:0] incrementador_de_2_bits_1_s0;

  Register #(.width(2), .Select("low")) register_1 (
    .D(incrementador_de_2_bits_1_s0), .en(Enable), .Q({q1, q0}), .clk(CLOCK_IN), .clr(Clear), .cs(1'b0),
    .preset(1'b0));
  Incrementador_de_2_bits incrementador_de_2_bits_1 (
    .s0(incrementador_de_2_bits_1_s0[0]), .s1(incrementador_de_2_bits_1_s0[1]), .a0(q0), .a1(q1));  // open: c0
endmodule

module Divisor_de_clock___divide_por_3 (
  input  Enable,
  output CLOCK_OUT
);

  wire CLOCK_IN_out, comparator_1_eq, comparator_1_gt;
  wire [1:0] contador_de_2_bits_1_q0;

  Clock CLOCK_IN (.out(CLOCK_IN_out));
  Contador_de_2_bits contador_de_2_bits_1 (
    .Enable(Enable), .CLOCK_IN(CLOCK_IN_out), .q1(contador_de_2_bits_1_q0[1]),
    .q0(contador_de_2_bits_1_q0[0]), .Clear(comparator_1_gt));
  Comparator #(.width(2), .mode("unsigned")) comparator_1 (
    .a(contador_de_2_bits_1_q0), .b(2'b10), .gt(comparator_1_gt), .eq(comparator_1_eq));  // open: lt
  or or_1 (CLOCK_OUT, comparator_1_gt, comparator_1_eq);
  // Digital_Oscilloscope CLOCK_IN_em_cima__x_CLOCK_OUT_embaixo: pin names not known; wires that end beside it: CLOCK_IN_out, CLOCK_OUT
endmodule
