// Logisim project Controlador_P04.circ as structural Verilog: 2 circuits, main circuit main
module main (
  input  D,
  input  T,
  input  Z,
  input  W,
  input  Y,
  input  X,
  output L
);

  wire clock_1_out;
  wire [2:0] lc_estado_1_d0, register_1_q;

  LC_ESTADO lc_estado_1 (
    .q2(register_1_q[2]), .q1(register_1_q[1]), .q0(register_1_q[0]), .X(X), .Y(Y), .W(W), .Z(Z), .T(T),
    .D(D), .d2(lc_estado_1_d0[2]), .d1(lc_estado_1_d0[1]), .d0(lc_estado_1_d0[0]), .L(L));
  Register #(.width(3), .Select("low")) register_1 (
    .D(lc_estado_1_d0), .en(1'b1), .Q(register_1_q), .clk(clock_1_out));  // open: clr
  Clock clock_1 (.out(clock_1_out));
endmodule

module LC_ESTADO (
  input  q2,
  input  q1,
  input  q0,
  input  X,
  input  Y,
  input  W,
  input  Z,
  input  T,
  input  D,
  output d2,
  output d1,
  output d0,
  output L
);

  wire and_1_out, and_2_out, and_3_out, and_4_out, and_5_out, and_6_out, and_7_out, and_8_out, and_10_out,
       and_11_out, and_12_out, and_13_out, and_14_out, and_15_out, and_16_out, and_17_out, and_18_out,
       or_2_out, or_3_out, xnor_1_out;

  xnor xnor_1 (xnor_1_out, Y, Z);
  and and_1 (and_1_out, ~q2, ~q1, q0);  // AND_Gate
  and and_2 (and_2_out, q2, ~q1, ~q0);  // AND_Gate
  and and_3 (and_3_out, q2, ~q1, q0);  // AND_Gate
  and and_4 (and_4_out, xnor_1_out, and_1_out);
  and and_5 (and_5_out, and_2_out, ~D);  // AND_Gate
  and and_6 (and_6_out, and_3_out, ~T);  // AND_Gate
  xor xor_1 (L, q2, q1);
  or or_1 (d2, and_4_out, and_5_out, and_6_out);
  and and_7 (and_7_out, ~q2, ~q1, q0);  // AND_Gate
  and and_8 (and_8_out, Y, ~Z);  // AND_Gate
  and and_9 (d1, and_7_out, and_8_out);
  or or_2 (or_2_out, ~X, ~W);  // OR_Gate
  and and_10 (and_10_out, Y, Z);
  and and_11 (and_11_out, ~q2, ~q1, ~q0);  // AND_Gate
  and and_12 (and_12_out, ~q2, ~q1, q0);  // AND_Gate
  and and_13 (and_13_out, Y, ~Z, or_2_out);  // AND_Gate
  and and_14 (and_14_out, ~q2, q1);  // AND_Gate
  and and_15 (and_15_out, q2, ~q1, q0);  // AND_Gate
  and and_16 (and_16_out, and_15_out, ~T);  // AND_Gate
  and and_17 (and_17_out, and_11_out, T);
  or or_3 (or_3_out, and_13_out, and_10_out);
  and and_18 (and_18_out, and_12_out, or_3_out);
  or or_4 (d0, and_17_out, and_18_out, and_14_out, and_16_out);
endmodule
